# Fritzing sketch esquematico (saved by Fritzing 0.9.6b)

parts:
  Componente1 = RFID-RC522-v2
  U1 = NodeMCU V1.0
  Componente2 = LCD1602-I2C

nets:
  N1: Componente1.SDA, U1.D4
  N2: Componente1.SCK, U1.D5
  N3: Componente1.MOSI, U1.D7
  N4: Componente1.MISO, Componente1.IRQ, U1.D6
  GND: Componente1.GND, U1.GND, Componente2.GND
  N5: Componente1.RST, U1.D3
  3.3V: Componente1.3.3V, U1.3V3, Componente2.VCC
  N6: U1.D1, Componente2.SCL
  N7: U1.D2, Componente2.SDA

custom parts:
  RFID-RC522-v2: A simple China made RFID-RC522 Reader; do check the pin labels, as this is a MFRC522 based clone.
  NodeMCU V1.0: ESP8266 based NodeMCU
  LCD1602-I2C: A standard character display, usually with 2x16 characters. Comes in many colors with LCM1602 IIC attached.
